// Logisim project bee26_project2_EC2.circ as structural Verilog: 9 circuits, main circuit main
module main (
);

  wire alu_1_carry_out, ALU_Select, branch_1_jump_enable, Clear, Clock, clock_doubler_1_out_2, Halt, KEYWE,
       RAM_WE, register_1_q, RF_WE, Screen_WE, undriven;
  wire [2:0] Data_Choice, Jump_Type, RD, RS;
  wire [3:0] Display_Unit_digit1, Display_Unit_digit2, Display_Unit_digit3, Display_Unit_digit4, OperationALU;
  wire [6:0] KeyOut;
  wire [7:0] ALU_Out, branch_1_jump_target, Data, Immediate, multiplexer_2_out, PC1, pc_control_1_pc_out,
       RAM_Out, RD_Out, RS_Out;
  wire [15:0] rom_1_data;

  Multiplexer #(.select(3), .width(8), .enable("false")) multiplexer_1 (
    .in0(PC1), .in1(ALU_Out), .in2(RAM_Out), .in3(Immediate), .in4({1'b0, KeyOut}), .out(Data),
    .sel(Data_Choice));  // open: in5, in6, in7
  PC_Control pc_control_1 (
    .Clock(Clock), .Halt(Halt), .Jump_enable(branch_1_jump_enable), .Jump_Target(branch_1_jump_target),
    .PC_out(pc_control_1_pc_out), .PC_1_out(PC1));
  branch branch_1 (
    .Register_Out(RD_Out), .Immediate(Immediate), .Jump_type(Jump_Type), .Jump_enable(branch_1_jump_enable),
    .Jump_Target(branch_1_jump_target));
  Keyboard keyboard_1 (.clk(Clock), .re(KEYWE), .data(KeyOut));  // open: clr, avail
  Clock clock_1 (.out(Clock));
  LED u_Halt (.in(Halt));
  Register_File register_file_1 (
    .Clock(Clock), .WE(RF_WE), .Data(Data), .Dest_reg(RD), .Src_Reg(RS), .Dest_Reg_Out(RD_Out),
    .Src_Reg_Out(RS_Out));
  Display_Unit Display_Unit (
    .Clock(Clock), .Clear(Clear), .WE(Screen_WE), .Data(RD_Out), .Imm(Immediate),
    .Digit1(Display_Unit_digit1), .Digit2(Display_Unit_digit2), .Digit3(Display_Unit_digit3),
    .Digit4(Display_Unit_digit4));
  ROM #(.dataWidth(16)) rom_1 (.addr(pc_control_1_pc_out), .data(rom_1_data));  // open: sel
  Hex_Digit_Display hex_digit_display_1 (.value(Display_Unit_digit2));  // open: dp
  Hex_Digit_Display hex_digit_display_2 (.value(Display_Unit_digit1));  // open: dp
  Instruction_Decoder instruction_decoder_1 (
    .in_1(Clock), .in_2(rom_1_data), .Halt(Halt), .Jump_Type(Jump_Type), .Immediate(Immediate),
    .Screen_Clear(Clear), .Screen_WE(Screen_WE), .RF_WE(RF_WE), .RS(RS), .RD(RD),
    .OperationForALU(OperationALU), .RAM_WE(RAM_WE), .ALU_Select(ALU_Select), .Data_Choice(Data_Choice),
    .KeyRead(KEYWE));
  Hex_Digit_Display hex_digit_display_3 (.value(Display_Unit_digit4));  // open: dp
  Hex_Digit_Display hex_digit_display_4 (.value(Display_Unit_digit3));  // open: dp
  RAM #(.bus("separate")) ram_1 (
    .addr(RS_Out), .din(RD_Out), .data(RAM_Out), .str(RAM_WE), .clk(Clock));  // open: sel, ld, clr
  Multiplexer #(.width(8), .enable("false")) multiplexer_2 (
    .in0(RS_Out), .in1(Immediate), .out(multiplexer_2_out), .sel(ALU_Select));
  Clock_doubler clock_doubler_1 (.Clock(Clock), .out_2(clock_doubler_1_out_2));
  ALU alu_1 (
    .Carry_In(register_1_q), .A(RD_Out), .B(multiplexer_2_out), .Operation(OperationALU), .Result(ALU_Out),
    .Carry_Out(alu_1_carry_out));
  Mult_Div mult_div_1 (.Clock(clock_doubler_1_out_2), .Start(undriven));  // open: Operation, RD, RS, Imm, Done, Out
  Register #(.width(1)) register_1 (.D(alu_1_carry_out), .Q(register_1_q), .clk(Clock));  // open: en, clr

  // Notes on the sheet:
  //   contents of rom_1 (hex, n*v repeats v):
  //   e300 db00 1c00 2403 9404 5c03 dc0c 5c01 dc11 5c02 dc16 a800 5b40 db00 c300 5310 a81b 5b47 db00 c300
  //   5310 a81b 5b67 db00 c300 5310 a81b 1c00 2401 8904 4103 9404 8a04 4204 a00 901 a800
endmodule

module Register_File (
  input  Clock,
  input  WE,
  input  [7:0] Data,
  input  [2:0] Dest_reg,
  input  [2:0] Src_Reg,
  output [7:0] Dest_Reg_Out,
  output [7:0] Src_Reg_Out
);

  wire demultiplexer_1_out1, demultiplexer_1_out2, demultiplexer_1_out3, demultiplexer_1_out4,
       demultiplexer_1_out5, demultiplexer_1_out6, demultiplexer_1_out7;
  wire [7:0] register_1_q, register_2_q, register_3_q, register_4_q, register_5_q, register_6_q, register_7_q;

  Demultiplexer #(.select(3), .enable("false")) demultiplexer_1 (
    .out1(demultiplexer_1_out1), .out2(demultiplexer_1_out2), .out3(demultiplexer_1_out3),
    .out4(demultiplexer_1_out4), .out5(demultiplexer_1_out5), .out6(demultiplexer_1_out6),
    .out7(demultiplexer_1_out7), .in(WE), .sel(Dest_reg));  // open: out0
  Register register_1 (.D(Data), .en(demultiplexer_1_out1), .Q(register_1_q), .clk(Clock));  // open: clr
  Register register_2 (.D(Data), .en(demultiplexer_1_out2), .Q(register_2_q), .clk(Clock));  // open: clr
  Register register_3 (.D(Data), .en(demultiplexer_1_out3), .Q(register_3_q), .clk(Clock));  // open: clr
  Register register_4 (.D(Data), .en(demultiplexer_1_out4), .Q(register_4_q), .clk(Clock));  // open: clr
  Register register_5 (.D(Data), .en(demultiplexer_1_out5), .Q(register_5_q), .clk(Clock));  // open: clr
  Register register_6 (.D(Data), .en(demultiplexer_1_out6), .Q(register_6_q), .clk(Clock));  // open: clr
  Register register_7 (.D(Data), .en(demultiplexer_1_out7), .Q(register_7_q), .clk(Clock));  // open: clr
  Multiplexer #(.select(3), .width(8), .enable("false")) multiplexer_1 (
    .in0({8{1'b0}}), .in1(register_1_q), .in2(register_2_q), .in3(register_3_q), .in4(register_4_q),
    .in5(register_5_q), .in6(register_6_q), .in7(register_7_q), .out(Dest_Reg_Out), .sel(Dest_reg));
  Multiplexer #(.select(3), .width(8), .enable("false")) multiplexer_2 (
    .in0({8{1'b0}}), .in1(register_1_q), .in2(register_2_q), .in3(register_3_q), .in4(register_4_q),
    .in5(register_5_q), .in6(register_6_q), .in7(register_7_q), .out(Src_Reg_Out), .sel(Src_Reg));

  // Other names for the same wires on the sheet: Select[2:0] = Dest_reg; Select2[2:0] = Src_Reg
endmodule

module ALU (
  input  Carry_In,
  input  [7:0] A,
  input  [7:0] B,
  input  [3:0] Operation,
  output [7:0] Result,
  output Carry_Out
);

  wire _1___Out, _2___Out, _3___Out, adder_2_cout, subtractor_3_bout, subtractor_4_bout;
  wire [7:0] adder_1_out, adder_2_out, and_1_out, not_1_out, or_1_out, shifter_1_out, shifter_2_out,
       subtractor_1_out, subtractor_2_out, subtractor_3_out, subtractor_4_out;

  Adder adder_1 (.a(A), .b(B), .out(adder_1_out), .cout(_1___Out));  // open: cin
  Subtractor subtractor_1 (.a(A), .b(B), .out(subtractor_1_out), .bout(_2___Out));  // open: bin
  Subtractor subtractor_2 (.a(B), .b(A), .out(subtractor_2_out), .bout(_3___Out));  // open: bin
  assign and_1_out = A & B;  // AND_Gate and_1, 8 bits wide
  assign or_1_out = A | B;  // OR_Gate or_1, 8 bits wide
  assign not_1_out = ~B;  // NOT_Gate not_1, 8 bits wide
  Adder adder_2 (.a(A), .b(B), .out(adder_2_out), .cin(Carry_In), .cout(adder_2_cout));
  Subtractor subtractor_3 (.a(A), .b(B), .out(subtractor_3_out), .bin(Carry_In), .bout(subtractor_3_bout));
  Subtractor subtractor_4 (.a(B), .b(A), .out(subtractor_4_out), .bin(Carry_In), .bout(subtractor_4_bout));
  Shifter shifter_1 (.in(A), .\dist (B[2:0]), .out(shifter_1_out));
  Shifter #(.shift("lr")) shifter_2 (.in(A), .\dist (B[2:0]), .out(shifter_2_out));
  Multiplexer #(.select(4), .width(8), .enable("false")) multiplexer_1 (
    .in0(adder_1_out), .in1(subtractor_1_out), .in2(subtractor_2_out), .in3(and_1_out), .in4(or_1_out),
    .in5(not_1_out), .in6(adder_2_out), .in7(subtractor_3_out), .in8(subtractor_4_out), .in9(shifter_1_out),
    .in10(shifter_2_out), .out(Result), .sel(Operation));  // open: in11, in12, in13, in14, in15
  Multiplexer #(.select(4), .enable("false")) multiplexer_2 (
    .in0(_1___Out), .in1(_2___Out), .in2(_3___Out), .in3(1'b0), .in4(1'b0), .in5(1'b0), .in6(adder_2_cout),
    .in7(subtractor_3_bout), .in8(subtractor_4_bout), .in9(1'b0), .in10(1'b0), .in11(1'b0), .in12(1'b0),
    .in13(1'b0), .in14(1'b0), .in15(1'b0), .out(Carry_Out), .sel(Operation));
endmodule

module Display_Unit (
  input  Clock,
  input  Clear,
  input  WE,
  input  [7:0] Data,
  input  [7:0] Imm,
  output [3:0] Digit1,
  output [3:0] Digit2,
  output [3:0] Digit3,
  output [3:0] Digit4
);

  wire and_1_out, and_2_out, and_3_out, comparator_1_eq, comparator_2_eq, HiControl, or_1_out;
  wire [7:0] multiplexer_1_out, multiplexer_2_out, register_1_q;

  and and_1 (and_1_out, WE, Clear);
  Comparator comparator_1 (.a(Imm), .b(8'h1), .eq(comparator_1_eq));  // open: gt, lt
  Register register_1 (.D(multiplexer_1_out), .en(HiControl), .Q(register_1_q), .clk(Clock));  // open: clr
  Multiplexer #(.width(8), .enable("false")) multiplexer_1 (
    .in0(Data), .in1({8{1'b0}}), .out(multiplexer_1_out), .sel(and_1_out));
  or or_1 (or_1_out, and_1_out, and_2_out);
  Comparator comparator_2 (.a(Imm), .b({8{1'b0}}), .eq(comparator_2_eq));  // open: gt, lt
  Multiplexer #(.width(8), .enable("false")) multiplexer_2 (
    .in0(register_1_q), .in1({8{1'b0}}), .out(multiplexer_2_out), .sel(and_1_out));
  Register register_2 (.D(multiplexer_2_out), .en(or_1_out), .Q({Digit1, Digit2}), .clk(Clock));  // open: clr
  Register register_3 (.D(multiplexer_1_out), .en(or_1_out), .Q({Digit3, Digit4}), .clk(Clock));  // open: clr
  and and_2 (and_2_out, WE, comparator_1_eq);
  and and_3 (and_3_out, WE, comparator_2_eq);
  or or_2 (HiControl, and_1_out, and_3_out);
endmodule

module Instruction_Decoder (
  input  in_1,
  input  [15:0] in_2,
  output Halt,
  output [2:0] RS,
  output [2:0] RD,
  output [2:0] Jump_Type,
  output RF_WE,
  output [7:0] Immediate,
  output Screen_WE,
  output Screen_Clear,
  output RAM_WE,
  output [3:0] OperationForALU,
  output ALU_Select,
  output [2:0] Data_Choice,
  output KeyRead
);

  wire comparator_3_eq;

  Multiplexer #(.select(5), .enable("false")) multiplexer_1 (
    .in0(1'b0), .in1(1'b0), .in2(1'b0), .in3(1'b1), .in4(1'b1), .in5(1'b1), .in6(1'b1), .in7(1'b1),
    .in8(1'b1), .in9(1'b1), .in10(1'b1), .in11(1'b1), .in12(1'b1), .in13(1'b1), .in14(1'b1), .in15(1'b1),
    .in16(1'b1), .in17(1'b1), .in18(1'b1), .in19(1'b1), .in20(1'b0), .in21(1'b0), .in22(1'b0), .in23(1'b1),
    .in24(1'b0), .in25(1'b0), .in26(1'b0), .in27(1'b0), .in28(1'b1), .in29(1'b0), .in30(1'b0), .in31(1'b0),
    .out(RF_WE), .sel(in_2[15:11]));
  Multiplexer #(.select(5), .width(4), .enable("false")) multiplexer_2 (
    .in0(4'b1111), .in1(4'b1111), .in2(4'b1111), .in3(4'b1111), .in4(4'b0000), .in5(4'b0001), .in6(4'b0010),
    .in7(4'b0011), .in8(4'b0100), .in9(4'b0101), .in10(4'b0000), .in11(4'b0001), .in12(4'b0110),
    .in13(4'b0111), .in14(4'b1000), .in15(4'b1001), .in16(4'b1010), .in17(4'b1001), .in18(4'b1010),
    .in19(4'b1111), .in20(4'b1111), .in21(4'b1111), .in22(4'b1111), .in23(4'b1111), .in24(4'b1111),
    .in25(4'b1111), .in26(4'b1111), .in27(4'b1111), .in28(4'b1111), .in29(4'b1111), .in30(4'b1111),
    .in31(4'b1111), .out(OperationForALU), .sel(in_2[15:11]));
  Comparator #(.width(5)) comparator_1 (.a(in_2[15:11]), .b(5'b11100), .eq(KeyRead));  // open: gt, lt
  Comparator #(.width(5)) comparator_2 (.a(in_2[15:11]), .b({5{1'b0}}), .eq(Halt));  // open: gt, lt
  Multiplexer #(.select(5), .enable("false")) multiplexer_3 (
    .in0(1'b0), .in1(1'b0), .in2(1'b0), .in3(1'b0), .in4(1'b0), .in5(1'b0), .in6(1'b0), .in7(1'b0),
    .in8(1'b0), .in9(1'b0), .in10(1'b1), .in11(1'b1), .in12(1'b0), .in13(1'b0), .in14(1'b0), .in15(1'b0),
    .in16(1'b0), .in17(1'b1), .in18(1'b1), .in19(1'b0), .in20(1'b0), .in21(1'b0), .in22(1'b0), .in23(1'b0),
    .in24(1'b0), .in25(1'b0), .in26(1'b0), .in27(1'b0), .in28(1'b0), .in29(1'b0), .in30(1'b0), .in31(1'b0),
    .out(ALU_Select), .sel(in_2[15:11]));
  Multiplexer #(.select(5), .width(3), .enable("false")) multiplexer_4 (
    .in0(3'b000), .in1(3'b000), .in2(3'b000), .in3(3'b000), .in4(3'b000), .in5(3'b000), .in6(3'b000),
    .in7(3'b000), .in8(3'b000), .in9(3'b000), .in10(3'b000), .in11(3'b000), .in12(3'b000), .in13(3'b000),
    .in14(3'b000), .in15(3'b000), .in16(3'b000), .in17(3'b000), .in18(3'b000), .in19(3'b000), .in20(3'b000),
    .in21(3'b001), .in22(3'b010), .in23(3'b011), .in24(3'b100), .in25(3'b101), .in26(3'b110), .in27(3'b111),
    .in28(3'b000), .in29(3'b000), .in30(3'b000), .in31(3'b000), .out(Jump_Type), .sel(in_2[15:11]));
  Comparator #(.width(5)) comparator_3 (.a(in_2[15:11]), .b(5'b00001), .eq(comparator_3_eq));  // open: gt, lt
  Comparator #(.width(5)) comparator_4 (.a(in_2[15:11]), .b(5'b00010), .eq(Screen_Clear));  // open: gt, lt
  Comparator #(.width(5)) comparator_5 (.a(in_2[15:11]), .b(5'b10100), .eq(RAM_WE));  // open: gt, lt
  or or_1 (Screen_WE, comparator_3_eq, Screen_Clear);
  Multiplexer #(.select(5), .width(3), .enable("false")) multiplexer_5 (
    .in0(3'b000), .in1(3'b000), .in2(3'b000), .in3(3'b111), .in4(3'b001), .in5(3'b001), .in6(3'b001),
    .in7(3'b001), .in8(3'b001), .in9(3'b001), .in10(3'b001), .in11(3'b001), .in12(3'b001), .in13(3'b001),
    .in14(3'b001), .in15(3'b001), .in16(3'b001), .in17(3'b001), .in18(3'b001), .in19(3'b110), .in20(3'b000),
    .in21(3'b000), .in22(3'b000), .in23(3'b000), .in24(3'b000), .in25(3'b000), .in26(3'b000), .in27(3'b000),
    .in28(3'b100), .in29(3'b000), .in30(3'b000), .in31(3'b000), .out(Data_Choice), .sel(in_2[15:11]));

  assign Immediate = in_2[7:0];
  assign RD = in_2[10:8];
  assign RS = in_2[2:0];

  // Other names for the same wires on the sheet: Clock = in_1; RDR[2:0] = in_2[10:8]; Opcode[4:0] = in_2[15:11]
endmodule

module PC_Control (
  input  Clock,
  input  Halt,
  input  Jump_enable,
  input  [7:0] Jump_Target,
  output [7:0] PC_out,
  output [7:0] PC_1_out
);

  wire not_1_out;
  wire [7:0] multiplexer_1_out;

  not not_1 (not_1_out, Halt);
  Register PC (.D(multiplexer_1_out), .en(not_1_out), .Q(PC_out), .clk(Clock));  // open: clr
  Multiplexer #(.width(8), .enable("false")) multiplexer_1 (
    .in0(PC_1_out), .in1(Jump_Target), .out(multiplexer_1_out), .sel(Jump_enable));
  Adder adder_1 (.a(PC_out), .b(8'h1), .out(PC_1_out));  // open: cin, cout
endmodule

module branch (
  input  [7:0] Register_Out,
  input  [7:0] Immediate,
  input  [2:0] Jump_type,
  output Jump_enable,
  output [7:0] Jump_Target
);

  wire comparator_1_eq, comparator_1_gt, comparator_1_lt, Comparison, multiplexer_1_out, not_1_out;

  Comparator comparator_1 (
    .a(Register_Out), .b({8{1'b0}}), .gt(comparator_1_gt), .eq(comparator_1_eq), .lt(comparator_1_lt));
  Multiplexer #(.select(3), .enable("false")) multiplexer_1 (
    .in0(1'b0), .in1(1'b1), .in2(1'b1), .in3(1'b1), .in4(1'b1), .in5(1'b1), .in6(1'b1), .in7(1'b1),
    .out(multiplexer_1_out), .sel(Jump_type));
  not not_1 (not_1_out, comparator_1_eq);
  and and_1 (Jump_enable, multiplexer_1_out, Comparison);
  Multiplexer #(.select(3), .width(8), .enable("false")) multiplexer_2 (
    .in1(Immediate), .in2(Register_Out), .in3(Immediate), .in4(Immediate), .in5(Immediate), .in6(Immediate),
    .in7(Immediate), .out(Jump_Target), .sel(Jump_type));  // open: in0
  Multiplexer #(.select(3), .enable("false")) multiplexer_3 (
    .in0(1'b1), .in1(1'b1), .in2(1'b1), .in3(1'b1), .in4(comparator_1_gt), .in5(comparator_1_lt),
    .in6(not_1_out), .in7(comparator_1_eq), .out(Comparison), .sel(Jump_type));

  // Other names for the same wires on the sheet: J[2:0] = Jump_type
endmodule

module Mult_Div (
  input  Clock,
  input  Operation,
  input  Start,
  input  [7:0] RD,
  input  [7:0] RS,
  input  [7:0] Imm,
  output Done,
  output [7:0] Out
);

  wire not_1_out, not_2_out, not_3_out, or_1_out, PWE, S;
  wire [2:0] adder_2_out, register_4_q;
  wire [7:0] adder_1_out, multiplexer_1_out, multiplexer_2_out, register_1_q, shifter_1_out, shifter_2_out;
  wire [7:1] register_3_q;

  Shifter shifter_1 (.in(register_1_q), .\dist (3'b001), .out(shifter_1_out));
  Multiplexer #(.width(8), .enable("false")) multiplexer_1 (
    .in0(shifter_1_out), .in1(RD), .out(multiplexer_1_out), .sel(not_1_out));
  not not_1 (not_1_out, Start);
  Register register_1 (.D(multiplexer_1_out), .en(S), .Q(register_1_q), .clk(Clock));  // open: clr
  Register register_2 (.D(adder_1_out), .en(PWE), .Q(Out), .clk(Clock));  // open: clr
  Adder adder_1 (.a(register_1_q), .b(Out), .out(adder_1_out));  // open: cin, cout
  Shifter #(.shift("lr")) shifter_2 (.in({register_3_q, PWE}), .out(shifter_2_out));  // open: dist
  not not_2 (not_2_out, Done);
  Multiplexer #(.width(8), .enable("false")) multiplexer_2 (
    .in0(shifter_2_out), .in1(RS), .out(multiplexer_2_out), .sel(Start));
  or or_1 (or_1_out, Start, not_2_out);
  Register register_3 (.D(multiplexer_2_out), .en(S), .Q({register_3_q, PWE}), .clk(Clock));  // open: clr
  Register #(.width(3)) register_4 (.D(adder_2_out), .en(or_1_out), .Q(register_4_q), .clk(Clock));  // open: clr
  Adder #(.width(3)) adder_2 (.a(register_4_q), .b(3'b001), .out(adder_2_out));  // open: cin, cout
  nor nor_1 (Done, register_4_q[0], register_4_q[1], register_4_q[2]);
  not not_3 (not_3_out, register_4_q[0]);
  nor nor_2 (S, Done, not_3_out);
endmodule

module Clock_doubler (
  input  Clock,
  output out_2
);

  wire buffer_1_out, buffer_2_out, buffer_3_out, buffer_4_out, buffer_5_out, buffer_6_out, d_ff_1_q;

  buf buffer_1 (buffer_1_out, buffer_2_out);
  buf buffer_2 (buffer_2_out, buffer_5_out);
  buf buffer_3 (buffer_3_out, d_ff_1_q);
  buf buffer_4 (buffer_4_out, buffer_6_out);
  buf buffer_5 (buffer_5_out, buffer_4_out);
  buf buffer_6 (buffer_6_out, buffer_3_out);
  xor xor_1 (out_2, buffer_1_out, Clock);
  D_Flip_Flop d_ff_1 (.clk(out_2), .D(Clock), .Q(d_ff_1_q));  // open: Qn, preset, en, reset
endmodule
